# Fritzing sketch solder_exhaust_fan (saved by Fritzing 0.9.3b)
breadboards: 1
perfboards: 1

parts:
  Part1 = Adafruit Metro Mini [part_number="Adafruit #2590"]
  C2 = Electrolytic Capacitor [capacitance=10µF voltage=50V package="100 mil [THT, electrolytic]"]
  C3 = Ceramic Capacitor [capacitance=0.1µF package="1206 [SMD, multilayer]"]
  Part2 = PowerBoost 1000 Basic
  neopixel1 = Neopixel Ring 16
  BAT1 = LIPO-2000mAh [package=lipo-2000]  # not connected
  Pushbutton = Momentary Switch [package=ksa_sealed_tac_switch]
  D1 = Rectifier Diode [part_number=1N4001 package="300 mil [THT]"]  # not connected
  SPDT_Switch = Toggle Switch [package=THT]
  5v_PC_Fan = DC Motor
  R1 = Resistor [tolerance=±0.5% resistance=1k package=THT]

nets:
  N1: Part1.IO10, Pushbutton.4
  N2: Part1.IO9, Part2.ENABLE
  N3: Part1.IO8, Part2.LBO
  N4: Part1.IO1, neopixel1.IN
  GND: Part1.GND, C2.-, C3.1, Part2.GND, neopixel1.GND, SPDT_Switch.COM, R1.Pin_0
  N5: Part1.VIN, Part2.VBAT
  N6: C2.+, C3.0, Part2.5.0V, neopixel1.VCC, Pushbutton.1, 5v_PC_Fan.pin_2
  N7: Pushbutton.3, R1.Pin_1

custom parts:
  Adafruit Metro Mini: We sure love the ATmega328 here at Adafruit, and we use them a lot for our own projects. The processor has plenty of GPIO, Analog inputs, hardware UART SPI and I2C, timers and PWM galore - just enough for most simple projects. When we need to go small, we use a Pro Trinket 3V or 5V, but if you want to have USB-to-Serial built in, we reach for an Adafruit METRO Mini. METRO Mini is the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
  PowerBoost 1000 Basic: The PowerBoost 1000 is a little DC/DC boost converter module that can run from 1.8V batteries or higher, and convert the battery output to 5.2V DC for running your 5V projects. At its heart is a TPS61030 boost converter from TI. This boost converter chip has some really nice extras such as low battery detection, 4A internal switch, synchronous conversion, excellent efficiency, and 700KHz high-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
  Neopixel Ring 16: Neopixel Ring x16
